# Fritzing sketch arduino-meter (saved by Fritzing 0.9.3b)

parts:
  U1 = ESP32-38PinWide [part_number=ESP32-38PinWide]
  M1 = MAX485 Breakout [package=THT]
  J1 = Screw terminal - 2 pins [package=THT]
  J2 = Screw terminal - 2 pins [package=THT]
  J3 = Screw terminal - 2 pins [package=THT]
  J4 = Screw terminal - 2 pins [package=THT]
  J5 = Screw terminal - 2 pins [package=THT]
  J6 = Screw terminal - 2 pins [package=THT]
  J7 = Screw terminal - 2 pins [package=THT]
  J8 = Screw terminal - 2 pins [package=THT]

nets:
  N1: U1.GPIO32, J8.pin2
  N2: U1.GPIO33, J5.pin2
  N3: U1.GPIO25, J6.pin2
  N4: U1.GPIO26, J7.pin2
  GND: U1.GND, M1.GND, J5.pin1, J6.pin1, J7.pin1, J8.pin1
  VIN: U1.VIN, M1.VCC
  N5: U1.GPIO4, M1.RE, M1.DE
  N6: U1.GPIO22, M1.RO
  N7: U1.GPIO23, M1.DI
  N8: M1.A, J1.pin2, J2.pin2, J3.pin2, J4.pin2
  N9: M1.B, J1.pin1, J2.pin1, J3.pin1, J4.pin1

custom parts:
  ESP32-38PinWide: Generic 38-Pin ESP32 with wide format (only access to one side of pins on a breadboard) based on Stephen Lilley's HiLetgo ESP-WROOM-32 ESP32 ESP-32S Development Board.
  MAX485 Breakout: MAX485 RS485 breakout board
