# Fritzing sketch tb74 (saved by Fritzing 0.9.3b)

parts:
  U1 = ESP32-38PinWide [part_number=ESP32-38PinWide]
  U2 = Sharp PC817 [package=THT]
  R1 = Resistor [tolerance=±5% resistance=1k package=THT]
  M1 = RioRand LM2596
  R2 = Resistor [tolerance=±5% resistance=10k package=THT]
  J1 = Screw terminal - 2 pins [package=THT]
  J2 = Screw terminal - 2 pins [package=THT]
  A1 = Bill acceptor TB74-U

nets:
  N1: U1.3.3, R2.Pin_1
  N2: U1.GND, U2.Pin_3, M1.Pin_4, J1.pin2, A1.Pin_4, A1.Pin_5, A1.Pin_6, A1.Pin_10
  N3: U1.GPIO5, J2.pin1, A1.Pin_2
  N4: U1.GPIO23, U2.Pin_4, R2.Pin_0
  N5: U2.Pin_1, R1.Pin_1
  N6: U2.Pin_2, J2.pin2, A1.Pin_1
  N7: R1.Pin_0, M1.Pin_3, J1.pin1
  N8: M1.Pin_1, A1.Pin_3

custom parts:
  ESP32-38PinWide: Generic 38-Pin ESP32 with wide format (only access to one side of pins on a breadboard) based on Stephen Lilley's HiLetgo ESP-WROOM-32 ESP32 ESP-32S Development Board.
  Bill acceptor TB74-U: The TB-Series is the latest generation of banknote reader designed exclusively by TOPVME with the highest safety and acceptance rate have over 96%.
